// Logisim project Lock.circ as structural Verilog: 6 circuits, main circuit NewPass1
// LCD
module main (
  input  Fire_alarm,
  input  Show_records,
  input  Record_of_emergency_openings,
  input  Set_Password,
  input  Enter_Password,
  input  Check_Password,
  output Lock,
  output Burglar_alarm,
  output out_9
);

  wire _0_out, _1_out, _2_out, _3_out, _4_out, _5_out, _6_out, _7_out, _8_out, _9_out, and_1_out,
       lock_1_alarm_2, not_1_out, Renter_password_out;
  wire [3:0] lock_1_wrong_attempts;

  Hex_Digit_Display hex_digit_display_1 (.value(lock_1_wrong_attempts));  // open: dp
  Button _0 (.out(_0_out));
  _7_Segment_Display u_7_segment_display_1 (.b(and_1_out), .c(and_1_out));  // open: g, f, a, e, d, dp
  and and_1 (and_1_out, not_1_out, Check_Password);
  Button _1 (.out(_1_out));
  _7_Segment_Display u_7_segment_display_2 (
    .f(and_1_out), .a(and_1_out), .b(and_1_out), .e(and_1_out), .c(and_1_out));  // open: g, d, dp
  not not_1 (not_1_out, Lock);
  Button _2 (.out(_2_out));
  _7_Segment_Display u_7_segment_display_3 (
    .f(Check_Password), .a(Check_Password), .b(Check_Password), .e(Check_Password), .d(Check_Password),
    .c(Check_Password));  // open: g, dp
  _7_Segment_Display u_7_segment_display_4 (
    .f(Check_Password), .a(Check_Password), .e(Check_Password), .d(Check_Password));  // open: g, b, c, dp
  lock lock_1 (
    ._0(_0_out), ._1(_1_out), ._2(_2_out), ._3(_3_out), ._4(_4_out), ._5(_5_out), ._6(_6_out), ._7(_7_out),
    ._8(_8_out), ._9(_9_out), .Set_password(Set_Password), .Renter_password(Renter_password_out),
    .Enter_password(Enter_Password), .Check_password(Check_Password), .Fire_alarm(Fire_alarm),
    .Alarm(lock_1_alarm_2), .Lock_output(Lock), .Burglar_alarm(Burglar_alarm), .Alarm_2(lock_1_alarm_2),
    .Second_Password(out_9), .Wrong_attempts(lock_1_wrong_attempts));
  Button _3 (.out(_3_out));
  Button _4 (.out(_4_out));
  _7_Segment_Display u_7_segment_display_5 (
    .f(Check_Password), .a(Check_Password), .e(Check_Password));  // open: g, b, d, c, dp
  Button _5 (.out(_5_out));
  _7_Segment_Display u_7_segment_display_6 (
    .f(Check_Password), .a(Check_Password), .e(Check_Password));  // open: g, b, d, c, dp
  Button _6 (.out(_6_out));
  _7_Segment_Display u_7_segment_display_7 (
    .g(Check_Password), .f(Check_Password), .a(Check_Password), .b(Check_Password), .e(Check_Password),
    .d(Check_Password));  // open: c, dp
  _7_Segment_Display u_7_segment_display_8 (
    .f(Check_Password), .a(Check_Password), .e(Check_Password), .d(Check_Password));  // open: g, b, c, dp
  Button _7 (.out(_7_out));
  Button Renter_password (.out(Renter_password_out));
  _7_Segment_Display u_7_segment_display_9 (
    .g(Check_Password), .f(Check_Password), .e(Check_Password), .d(Check_Password));  // open: a, b, c, dp
  Button _8 (.out(_8_out));
  Button _9 (.out(_9_out));
  LED Alarm (.in(lock_1_alarm_2));

  assign Show_records = Record_of_emergency_openings;

  // Other names for the same wires on the sheet: LCD = Record_of_emergency_openings

  // Notes on the sheet:
  //   LCD SCREEN WHERE PAST 10 RECORDS
  //   WILL BE SHOWN
  //   Number of wrong attempts
  //   ENTER A 5 DIGIT PASSWORD
  //   ENHANCED SECURITY LOCKING SYSTEM
  //   INSTRUCTIONS
  //   -> TO ENTER A NEW PASSWORD PRESS THE "RE-ENTER" BUTTON
  //   ->AFTER 3 WRONG ATTEMPTS AN ALARM WILL TURN ON
  //   -> TO TURN OFF THE ALARM ENTER THE PASSWORD REQUIRED
  //   -> TO CHECK IF ENTERED PASSWORD IS CORRECT, SWITCH "CHECK PASSWORD" ON 
  //   ->TO ENTER A PASSWORD, SWITCH "ENTER PASSWORD" ON, AFTER WHICH ENTER A 5 DIGIT PASSWORD
endmodule

// Reset password
module NewPass1 (
  input  _0,
  input  _1,
  input  _2,
  input  _3,
  input  _4,
  input  _5,
  input  _6,
  input  _7,
  input  _8,
  input  _9,
  input  Set,
  output [3:0] P1,
  output [3:0] P2,
  output [3:0] P3,
  output [3:0] P4,
  output [3:0] P5
);

  wire and_1_out, demultiplexer_2_out1, demultiplexer_2_out2, demultiplexer_2_out3, demultiplexer_2_out4,
       demultiplexer_2_out5, multiplexer_1_out, or_1_out;
  wire [2:0] counter_1_q;
  wire [3:0] demultiplexer_1_out1, demultiplexer_1_out2, demultiplexer_1_out3, demultiplexer_1_out4,
       demultiplexer_1_out5, priority_encoder_1_out;

  or or_1 (or_1_out, _0, _1, _2, _3, _4, _5, _6, _7, _8, _9);
  and and_1 (and_1_out, or_1_out, Set);
  Priority_Encoder #(.select(4)) priority_encoder_1 (
    .in0(_0), .in1(_1), .in2(_2), .in3(_3), .in4(_4), .in5(_5), .in6(_6), .in7(_7), .in8(_8), .in9(_9),
    .out(priority_encoder_1_out), .en_in(and_1_out));  // open: in10, in11, in12, in13, in14, in15, gs, en_out
  Counter #(.width(3), .max('h7)) counter_1 (
    .count(and_1_out), .Q(counter_1_q), .clk(and_1_out), .clr(multiplexer_1_out));  // open: load, D, carry
  Multiplexer #(.select(3), .enable("false")) multiplexer_1 (
    .in0(1'b0), .in1(1'b0), .in2(1'b0), .in3(1'b0), .in4(1'b0), .in5(1'b0), .in6(1'b1), .in7(1'b0),
    .out(multiplexer_1_out), .sel(counter_1_q));
  Demultiplexer #(.select(3), .width(4)) demultiplexer_1 (
    .out1(demultiplexer_1_out1), .out2(demultiplexer_1_out2), .out3(demultiplexer_1_out3),
    .out4(demultiplexer_1_out4), .out5(demultiplexer_1_out5), .in(priority_encoder_1_out), .sel(counter_1_q),
    .en(and_1_out));  // open: out0, out6, out7
  Register #(.width(4)) register_1 (
    .D(demultiplexer_1_out1), .en(demultiplexer_2_out1), .Q(P1), .clk(demultiplexer_2_out1),
    .clr(multiplexer_1_out));
  Register #(.width(4)) register_2 (
    .D(demultiplexer_1_out2), .en(demultiplexer_2_out2), .Q(P2), .clk(demultiplexer_2_out2),
    .clr(multiplexer_1_out));
  Register #(.width(4)) register_3 (
    .D(demultiplexer_1_out3), .en(demultiplexer_2_out3), .Q(P3), .clk(demultiplexer_2_out3),
    .clr(multiplexer_1_out));
  Register #(.width(4)) register_4 (
    .D(demultiplexer_1_out4), .en(demultiplexer_2_out4), .Q(P4), .clk(demultiplexer_2_out4),
    .clr(multiplexer_1_out));
  Register #(.width(4)) register_5 (
    .D(demultiplexer_1_out5), .en(demultiplexer_2_out5), .Q(P5), .clk(demultiplexer_2_out5),
    .clr(multiplexer_1_out));
  Demultiplexer #(.select(3)) demultiplexer_2 (
    .out1(demultiplexer_2_out1), .out2(demultiplexer_2_out2), .out3(demultiplexer_2_out3),
    .out4(demultiplexer_2_out4), .out5(demultiplexer_2_out5), .in(1'b1), .sel(counter_1_q), .en(and_1_out));  // open: out0, out6, out7

  // Notes on the sheet:
  //   Digit counter
  //   TO SET NEW PASSWORD
endmodule

// LOCK
module lock (
  input  _0,
  input  _1,
  input  _2,
  input  _3,
  input  _4,
  input  _5,
  input  _6,
  input  _7,
  input  _8,
  input  _9,
  input  Set_password,
  input  Renter_password,
  input  Enter_password,
  input  Check_password,
  input  Fire_alarm,
  input  Alarm,
  output Lock_output,
  output Burglar_alarm,
  output Alarm_2,
  output Second_Password,
  output [3:0] Wrong_attempts
);

  wire and_1_out, mainpass_1_lock_output, register_1_q;
  wire [3:0] newpass1_1_p1, newpass1_1_p2, newpass1_1_p3, newpass1_1_p4, newpass1_1_p5;

  and and_1 (and_1_out, Set_password, register_1_q);
  NewPass1 newpass1_1 (
    ._0(_0), ._1(_1), ._2(_2), ._3(_3), ._4(_4), ._5(_5), ._6(_6), ._7(_7), ._8(_8), ._9(_9),
    .Set(and_1_out), .P1(newpass1_1_p1), .P2(newpass1_1_p2), .P3(newpass1_1_p3), .P4(newpass1_1_p4),
    .P5(newpass1_1_p5));
  Register #(.width(1)) register_1 (
    .D(1'b1), .en(Lock_output), .Q(register_1_q), .clk(Lock_output), .clr(Enter_password));
  MainPass mainpass_1 (
    ._0(_0), ._1(_1), ._2(_2), .P1(newpass1_1_p1), ._3(_3), ._4(_4), ._5(_5), .P2(newpass1_1_p2), ._6(_6),
    ._7(_7), .P3(newpass1_1_p3), ._8(_8), ._9(_9), .P4(newpass1_1_p4), .P5(newpass1_1_p5),
    .Enter_password(Enter_password), .Renter_password(Renter_password), .Check_password(Check_password),
    .Lock_output(mainpass_1_lock_output));
  SecondPass secondpass_1 (
    ._0(_0), ._1(_1), ._2(_2), .P1(4'b0001), ._3(_3), ._4(_4), ._5(_5), .P2(4'b0001), ._6(_6), ._7(_7),
    .P3(4'b0010), ._8(_8), ._9(_9), .P4(4'b0010), .P5(4'b0010), .Renter_password(Renter_password),
    .Enter_password(Enter_password), .Alarm_on(Alarm), .Second_password_check(Second_Password));
  Alarms alarms_1 (
    .Fire_alarm(Fire_alarm), .Lock_output(mainpass_1_lock_output), .Second_password_check(Second_Password),
    .Password_entered(Check_password), .Lock_Output_2(Lock_output), .Burglar_alarm(Burglar_alarm),
    .Alarm(Alarm_2), .Wrong_attempts(Wrong_attempts));

  // Notes on the sheet:
  //   MAIN LOCK
endmodule

// Compare password1
module MainPass (
  input  _0,
  input  _1,
  input  _2,
  input  [3:0] P1,
  input  _3,
  input  _4,
  input  _5,
  input  [3:0] P2,
  input  _6,
  input  _7,
  input  [3:0] P3,
  input  _8,
  input  _9,
  input  [3:0] P4,
  input  [3:0] P5,
  input  Enter_password,
  input  Renter_password,
  input  Check_password,
  output Lock_output
);

  wire and_1_out, and_2_out, comparator_1_eq, comparator_2_eq, comparator_3_eq, comparator_4_eq,
       comparator_5_eq, demultiplexer_2_out1, demultiplexer_2_out2, demultiplexer_2_out3,
       demultiplexer_2_out4, demultiplexer_2_out5, multiplexer_1_out, or_1_out, or_2_out;
  wire [2:0] counter_1_q;
  wire [3:0] demultiplexer_1_out1, demultiplexer_1_out2, demultiplexer_1_out3, demultiplexer_1_out4,
       demultiplexer_1_out5, priority_encoder_1_out, register_1_q, register_2_q, register_3_q, register_4_q,
       register_5_q;

  or or_1 (or_1_out, _0, _1, _2, _3, _4, _5, _6, _7, _8, _9);
  and and_1 (and_1_out, or_1_out, Enter_password);
  Priority_Encoder #(.select(4)) priority_encoder_1 (
    .in0(_0), .in1(_1), .in2(_2), .in3(_3), .in4(_4), .in5(_5), .in6(_6), .in7(_7), .in8(_8), .in9(_9),
    .out(priority_encoder_1_out), .en_in(and_1_out));  // open: in10, in11, in12, in13, in14, in15, gs, en_out
  Counter #(.width(3), .max('h7)) counter_1 (
    .count(and_1_out), .Q(counter_1_q), .clk(and_1_out), .clr(or_2_out));  // open: load, D, carry
  or or_2 (or_2_out, Renter_password, multiplexer_1_out);
  Demultiplexer #(.select(3), .width(4)) demultiplexer_1 (
    .out1(demultiplexer_1_out1), .out2(demultiplexer_1_out2), .out3(demultiplexer_1_out3),
    .out4(demultiplexer_1_out4), .out5(demultiplexer_1_out5), .in(priority_encoder_1_out), .sel(counter_1_q),
    .en(and_1_out));  // open: out0, out6, out7
  Multiplexer #(.select(3), .enable("false")) multiplexer_1 (
    .in0(1'b0), .in1(1'b0), .in2(1'b0), .in3(1'b0), .in4(1'b0), .in5(1'b0), .in6(1'b1), .in7(1'b0),
    .out(multiplexer_1_out), .sel(counter_1_q));
  Register #(.width(4)) register_1 (
    .D(demultiplexer_1_out1), .en(demultiplexer_2_out1), .Q(register_1_q), .clk(demultiplexer_2_out1),
    .clr(multiplexer_1_out));
  Register #(.width(4)) register_2 (
    .D(demultiplexer_1_out2), .en(demultiplexer_2_out2), .Q(register_2_q), .clk(demultiplexer_2_out2),
    .clr(multiplexer_1_out));
  Register #(.width(4)) register_3 (
    .D(demultiplexer_1_out3), .en(demultiplexer_2_out3), .Q(register_3_q), .clk(demultiplexer_2_out3),
    .clr(multiplexer_1_out));
  Register #(.width(4)) register_4 (
    .D(demultiplexer_1_out4), .en(demultiplexer_2_out4), .Q(register_4_q), .clk(demultiplexer_2_out4),
    .clr(multiplexer_1_out));
  Register #(.width(4)) register_5 (
    .D(demultiplexer_1_out5), .en(demultiplexer_2_out5), .Q(register_5_q), .clk(demultiplexer_2_out5),
    .clr(multiplexer_1_out));
  Demultiplexer #(.select(3)) demultiplexer_2 (
    .out1(demultiplexer_2_out1), .out2(demultiplexer_2_out2), .out3(demultiplexer_2_out3),
    .out4(demultiplexer_2_out4), .out5(demultiplexer_2_out5), .in(1'b1), .sel(counter_1_q), .en(and_1_out));  // open: out0, out6, out7
  Comparator #(.width(4)) comparator_1 (.a(register_1_q), .b(P1), .eq(comparator_1_eq));  // open: gt, lt
  Comparator #(.width(4)) comparator_2 (.a(register_2_q), .b(P2), .eq(comparator_2_eq));  // open: gt, lt
  Comparator #(.width(4)) comparator_3 (.a(register_3_q), .b(P3), .eq(comparator_3_eq));  // open: gt, lt
  Comparator #(.width(4)) comparator_4 (.a(register_4_q), .b(P4), .eq(comparator_4_eq));  // open: gt, lt
  Comparator #(.width(4)) comparator_5 (.a(register_5_q), .b(P5), .eq(comparator_5_eq));  // open: gt, lt
  and and_2 (and_2_out, comparator_1_eq, comparator_2_eq, comparator_3_eq, comparator_4_eq, comparator_5_eq);
  and and_3 (Lock_output, and_2_out, Check_password);

  // Notes on the sheet:
  //   Digit counter
  //   MAIN LOCK CIRCUIT
endmodule

// Compare password2
module SecondPass (
  input  _0,
  input  _1,
  input  _2,
  input  [3:0] P1,
  input  _3,
  input  _4,
  input  _5,
  input  [3:0] P2,
  input  _6,
  input  _7,
  input  [3:0] P3,
  input  _8,
  input  _9,
  input  [3:0] P4,
  input  [3:0] P5,
  input  Renter_password,
  input  Enter_password,
  input  Alarm_on,
  output Second_password_check
);

  wire and_1_out, and_2_out, comparator_1_eq, comparator_2_eq, comparator_3_eq, comparator_4_eq,
       comparator_5_eq, demultiplexer_2_out1, demultiplexer_2_out2, demultiplexer_2_out3,
       demultiplexer_2_out4, demultiplexer_2_out5, multiplexer_1_out, or_1_out, or_2_out;
  wire [2:0] counter_1_q;
  wire [3:0] demultiplexer_1_out1, demultiplexer_1_out2, demultiplexer_1_out3, demultiplexer_1_out4,
       demultiplexer_1_out5, priority_encoder_1_out, register_1_q, register_2_q, register_3_q, register_4_q,
       register_5_q;

  or or_1 (or_1_out, _0, _1, _2, _3, _4, _5, _6, _7, _8, _9);
  or or_2 (or_2_out, Renter_password, multiplexer_1_out);
  and and_1 (and_1_out, or_1_out, Enter_password);
  Priority_Encoder #(.select(4)) priority_encoder_1 (
    .in0(_0), .in1(_1), .in2(_2), .in3(_3), .in4(_4), .in5(_5), .in6(_6), .in7(_7), .in8(_8), .in9(_9),
    .out(priority_encoder_1_out), .en_in(and_1_out));  // open: in10, in11, in12, in13, in14, in15, gs, en_out
  Counter #(.width(3), .max('h7)) counter_1 (
    .count(and_1_out), .Q(counter_1_q), .clk(and_1_out), .clr(or_2_out));  // open: load, D, carry
  Demultiplexer #(.select(3), .width(4)) demultiplexer_1 (
    .out1(demultiplexer_1_out1), .out2(demultiplexer_1_out2), .out3(demultiplexer_1_out3),
    .out4(demultiplexer_1_out4), .out5(demultiplexer_1_out5), .in(priority_encoder_1_out), .sel(counter_1_q),
    .en(and_1_out));  // open: out0, out6, out7
  Multiplexer #(.select(3), .enable("false")) multiplexer_1 (
    .in0(1'b0), .in1(1'b0), .in2(1'b0), .in3(1'b0), .in4(1'b0), .in5(1'b0), .in6(1'b1), .in7(1'b0),
    .out(multiplexer_1_out), .sel(counter_1_q));
  Register #(.width(4)) register_1 (
    .D(demultiplexer_1_out1), .en(demultiplexer_2_out1), .Q(register_1_q), .clk(demultiplexer_2_out1),
    .clr(multiplexer_1_out));
  Register #(.width(4)) register_2 (
    .D(demultiplexer_1_out2), .en(demultiplexer_2_out2), .Q(register_2_q), .clk(demultiplexer_2_out2),
    .clr(multiplexer_1_out));
  Register #(.width(4)) register_3 (
    .D(demultiplexer_1_out3), .en(demultiplexer_2_out3), .Q(register_3_q), .clk(demultiplexer_2_out3),
    .clr(multiplexer_1_out));
  Register #(.width(4)) register_4 (
    .D(demultiplexer_1_out4), .en(demultiplexer_2_out4), .Q(register_4_q), .clk(demultiplexer_2_out4),
    .clr(multiplexer_1_out));
  Register #(.width(4)) register_5 (
    .D(demultiplexer_1_out5), .en(demultiplexer_2_out5), .Q(register_5_q), .clk(demultiplexer_2_out5),
    .clr(multiplexer_1_out));
  Demultiplexer #(.select(3)) demultiplexer_2 (
    .out1(demultiplexer_2_out1), .out2(demultiplexer_2_out2), .out3(demultiplexer_2_out3),
    .out4(demultiplexer_2_out4), .out5(demultiplexer_2_out5), .in(1'b1), .sel(counter_1_q), .en(and_1_out));  // open: out0, out6, out7
  Comparator #(.width(4)) comparator_1 (.a(register_1_q), .b(P1), .eq(comparator_1_eq));  // open: gt, lt
  Comparator #(.width(4)) comparator_2 (.a(register_2_q), .b(P2), .eq(comparator_2_eq));  // open: gt, lt
  Comparator #(.width(4)) comparator_3 (.a(register_3_q), .b(P3), .eq(comparator_3_eq));  // open: gt, lt
  Comparator #(.width(4)) comparator_4 (.a(register_4_q), .b(P4), .eq(comparator_4_eq));  // open: gt, lt
  Comparator #(.width(4)) comparator_5 (.a(register_5_q), .b(P5), .eq(comparator_5_eq));  // open: gt, lt
  and and_2 (and_2_out, comparator_1_eq, comparator_2_eq, comparator_3_eq, comparator_4_eq, comparator_5_eq);
  and and_3 (Second_password_check, and_2_out, Alarm_on);

  // Notes on the sheet:
  //   Digit counter
  //   CIRCUIT TO TURN OFF ALARM
endmodule

module Alarms (
  input  Fire_alarm,
  input  Lock_output,
  input  Second_password_check,
  input  Password_entered,
  output Lock_Output_2,
  output Burglar_alarm,
  output Alarm,
  output [3:0] Wrong_attempts
);

  wire and_1_out, not_1_out, not_2_out, not_3_out, or_2_out;

  not not_1 (not_1_out, and_1_out);
  buf and_1 (and_1_out, Lock_output);  // AND_Gate
  or or_1 (Lock_Output_2, Fire_alarm, Lock_output);
  not not_2 (not_2_out, 1'b1);
  not not_3 (not_3_out, Lock_output);
  Counter #(.width(4), .max('hf), .ongoal("stay")) counter_1 (
    .count(not_1_out), .Q(Wrong_attempts), .clk(Password_entered), .clr(or_2_out));  // open: load, D, carry
  or or_2 (or_2_out, Lock_output, Second_password_check);
  and and_2 (Burglar_alarm, not_2_out, not_3_out);
  Multiplexer #(.select(4)) multiplexer_1 (
    .in0(1'b0), .in1(1'b0), .in2(1'b0), .in3(1'b1), .in4(1'b1), .in5(1'b1), .in6(1'b1), .in7(1'b1),
    .in8(1'b1), .in9(1'b1), .in10(1'b1), .in11(1'b1), .in12(1'b1), .in13(1'b1), .in14(1'b1), .in15(1'b1),
    .out(Alarm), .sel(Wrong_attempts), .en(1'b1));
  Hex_Digit_Display hex_digit_display_1 (.value(Wrong_attempts));  // open: dp

  // Notes on the sheet:
  //   Latch circuit
  //   Wrong attempt
  //   counter
  //   ALARMS AND OUTPUT CIRCUIT
  //   Number of wrong attempts
endmodule
